// Logisim project MIPS.circ as structural Verilog: 6 circuits, main circuit MIPS
module MIPS (
  input  [31:0] in_1
);

  wire mipsprogramrom_1_p1, registerfile_1_p1, registerfile_1_p2;

  // Incrementer incrementer_1: pin names not known
  // Mips_ALU mips_alu_1: pin names not known; wires that end beside it: in_1
  // MIPSProgramROM mipsprogramrom_1: pin names not known; wires that end beside it: mipsprogramrom_1_p1, mipsprogramrom_1_p1
  Multiplexer multiplexer_1 ();  // open: in0, in1, out, sel, en
  // LCD_Video lcd_video_1: pin names not known
  // MIPS_RAM mips_ram_1: pin names not known
  // RegisterFile registerfile_1: pin names not known; wires that end beside it: registerfile_1_p1, registerfile_1_p2, registerfile_1_p1, registerfile_1_p2
endmodule

module Fetch (
  input  [31:0] in_1,
  output [31:0] out_2
);

  // MIPS_RAM mips_ram_1: pin names not known
  // RegisterFile registerfile_1: pin names not known
  // MIPSProgramROM mipsprogramrom_1: pin names not known; wires that end beside it: in_1, out_2
endmodule

module Decode (
);

  // RegisterFile registerfile_1: pin names not known
  Comparator comparator_1 ();  // open: a, b, gt, eq, lt
endmodule

module Execute (
  input  RegisterFileD,
  input  [4:0] A,
  input  [4:0] B,
  input  [15:0] Immediate,
  input  [4:0] Rd,
  input  [4:0] Rb,
  input  [4:0] Ra,
  output RegisterFileD_2,
  output [4:0] D,
  output [4:0] B_2,
  output [4:0] Rd_2,
  output WE,
  output MC
);

  wire multiplexer_1_out;
  wire [31:0] mips_alu_1_p2;

  Multiplexer multiplexer_1 (.out(multiplexer_1_out));  // open: in0, in1, sel, en
  Multiplexer multiplexer_2 ();  // open: in0, in1, out, sel, en
  Multiplexer multiplexer_3 ();  // open: in0, in1, out, sel, en
  // Mips_ALU mips_alu_1: pin names not known; wires that end beside it: multiplexer_1_out, mips_alu_1_p2

  assign RegisterFileD_2 = RegisterFileD;
endmodule

module Memory (
  input  RegisterFileD,
  input  [4:0] D,
  input  B,
  input  Rd,
  input  WE,
  input  MC,
  output RegisterFileD_2,
  output [4:0] D_2,
  output M,
  output Rd_2,
  output WE_2,
  output MC_2
);


  assign RegisterFileD_2 = RegisterFileD;
endmodule

module Writeback (
  input  D,
  input  M,
  input  Rd,
  input  WE,
  input  MC,
  output RegisterFileD
);

  Multiplexer multiplexer_1 (.out(RegisterFileD));  // open: in0, in1, sel, en
endmodule
